# Fritzing sketch shutter-timer (saved by Fritzing 0.8.7b)
breadboards: 1

parts:
  Part1 = Arduino Uno (Rev3)
  LED1 = LED - 3mm [color="Red (633nm)" package="3 mm [THT]"]
  R1 = Resistor [tolerance=±5% resistance=220 package=THT]
  LED2 = LED - 3mm [color="Infrared (940nm)" package="3 mm [THT]"]
  R3 = Resistor [tolerance=±5% resistance=10k package=THT]
  R2 = Resistor [tolerance=±5% resistance=1k package=THT]

nets:
  N1: Part1.D2, R2.Pin_1
  N2: Part1.5V, LED1.anode, R3.Pin_0
  N3: Part1.GND, R1.Pin_1, LED2.cathode
  N4: LED1.cathode, R1.Pin_0
  N5: LED2.anode, R3.Pin_1, R2.Pin_0

notes:
  camera goes here
